# Fritzing sketch ComputerHeatMonitor (saved by Fritzing 0.9.4)
breadboards: 1

parts:
  Parça1 = Arduino Uno (Rev3)
  T1 = LM35 Temperature Sensor [package="TO92 [THT]"]
  R6 = Resistor [tolerance=±5% resistance=10k package=THT]
  BT1 = Bluetooth HC-06d [package=THT]

nets:
  N1: Parça1.A0, T1.Vout
  N2: Parça1.D10_PWM/SS, BT1.TXD
  N3: Parça1.D11_PWM/MOSI, R6.Pin_0
  5V: Parça1.5V, T1.+Vs, BT1.VCC
  GND: Parça1.GND, T1.GND, BT1.GND
  N4: R6.Pin_1, BT1.RXD

custom parts:
  Bluetooth HC-06d: Bluetooth HC-06 - face down, pins down 16.5mm x 37.5mm PCB
